# Fritzing sketch deck (saved by Fritzing 0.9.1b)
breadboards: 1

parts:
  Part1 = Arduino Uno (Rev3)
  IC1 = L293D [package=THT]
  M1 = DC Motor

nets:
  N1: Part1.D2, IC1.Enable_1, IC1.+V
  N2: Part1.D4, IC1.In_1
  N3: Part1.D7, IC1.In_2
  N4: Part1.GND, IC1.0V
  N5: IC1.Out_1_(_Controlled_by_Enable_1_), M1.pin_1
  N6: IC1.Out_2_(_Controlled_by_Enable_1_), M1.pin_2

notes:
  +12 V
  To HCSR04s Trig pin
  To HCSR04 ECHO pin
